# Fritzing sketch Diagrama_JavaArduino (saved by Fritzing 0.9.3b)
breadboards: 1

parts:
  Componente1 = Arduino Uno (Rev3) - ICSP
  LCD1 = LCD screen
  R1 = Rotary Potentiometer (Large) [maximum_resistance=100kΩ package=THT]
  RHT1 = Humidity and Temperature Sensor RHT03
  MH-Real-Time_Clock_Module_3 = RTC_DS1302_module
  Q1 = NPN-Transistor [package="SOT-23 [SMD]"]
  R2 = Resistor [tolerance=±5% resistance=220 package="2010 [SMD]"]
  R3 = Resistor [tolerance=±5% resistance=220 package="2010 [SMD]"]
  F1 = Fan - Ventilador [package=THT]
  R4 = Resistor [tolerance=±5% resistance=220 package="2010 [SMD]"]

nets:
  N1: Componente1.D8, LCD1.RS
  N2: Componente1.D9_PWM, LCD1.E
  N3: Componente1.D10_PWM/SS, LCD1.DB4
  N4: Componente1.D11_PWM/MOSI, LCD1.DB5
  N5: Componente1.D12/MISO, LCD1.DB6
  N6: Componente1.D13/SCK, LCD1.DB7
  N7: Componente1.D2, MH-Real-Time_Clock_Module_3.RST
  N8: Componente1.D3_PWM, MH-Real-Time_Clock_Module_3.DAT
  N9: Componente1.D4, MH-Real-Time_Clock_Module_3.CLK
  N10: Componente1.D5_PWM, R4.Pin_0
  N11: Componente1.D6_PWM, Q1.0
  VCC: Componente1.5V, LCD1.VDD, R1.leg2, RHT1.Vcc, MH-Real-Time_Clock_Module_3.VCC, R2.Pin_1, R3.Pin_1
  GND: Componente1.GND, LCD1.VSS, LCD1.R/W, LCD1.LED-, R1.leg1, RHT1.GND_2, MH-Real-Time_Clock_Module_3.GND, F1.GND
  N12: LCD1.V0, R1.wiper
  N13: LCD1.LED+, R2.Pin_0
  N14: Q1.2, F1.5V
  N15: Q1.1, R3.Pin_0

custom parts:
  RTC_DS1302_module: Arduino module DS1302 SPI Real Time Clock
  Fan - Ventilador: Ventilador de 2 pines, se encuentra comunmente en computadoras de escritorio
